# Fritzing sketch remy schematic (saved by Fritzing 1.0.4)
breadboards: 1

parts:
  R1 = Basic Flex Resistor
  R2 = Basic Force Sensing Resistor (FSR) [package=THT]
  Part2 = Adafruit DS3502
  U1 = POT [knob_status=50% power=0.5W package=pot_alpha_rv16af-20]
  R3 = Resistor [tolerance=±5% power=0.25W resistance=10 package=THT]
  R4 = Resistor [tolerance=±5% power=0.25W resistance=10 package=THT]
  VCC1 = 4 x AAA Battery Mount [internal_resistance=0.1Ω]  # not connected
  LED2 = DUO LED RG [package="5 mm [THT]"]
  A1 = Arduino UNO R4 WiFi
  Part1 = Arduino Uno (Rev3)

nets:
  N1: R1.Pin_2, R4.Pin_0, A1.Pin_12, Part1.A0
  GND: R1.pin_1, Part2.GND, LED2.green_anode, A1.Pin_2, A1.Pin_9, A1.Pin_10, A1.Pin_30, A1.Pin_48, Part1.GND
  N2: R2.pin_2, R3.Pin_0, A1.Pin_13, Part1.A1
  N3: Part2.RL, U1.A
  N4: Part2.RW, U1.S
  N5: Part2.RH, U1.E
  N6: Part2.VCC, R3.Pin_1, R4.Pin_1
  N7: LED2.red_anode, A1.Pin_44, Part1.D10_PWM/SS
  N8: LED2.common_cathode, A1.Pin_43, Part1.D9_PWM
  N9: A1.Pin_4, Part1.N/C
  N10: A1.Pin_5, Part1.ioref
  N11: A1.Pin_6, A1.Pin_22, A1.Pin_23, Part1.RESET
  N12: A1.Pin_7, Part1.3V3
  N13: A1.Pin_8, A1.Pin_27, Part1.5V
  N14: A1.Pin_11, Part1.VIN
  N15: A1.Pin_14, Part1.A2
  N16: A1.Pin_15, Part1.A3
  N17: A1.Pin_16, A1.Pin_50, Part1.A4/SDA
  N18: A1.Pin_17, A1.Pin_51, Part1.A5/SCL
  N19: A1.Pin_34, Part1.D0/RX
  N20: A1.Pin_35, Part1.D1/TX
  N21: A1.Pin_36, Part1.D2
  N22: A1.Pin_37, Part1.D3_PWM
  N23: A1.Pin_38, Part1.D4
  N24: A1.Pin_39, Part1.D5_PWM
  N25: A1.Pin_40, Part1.D6_PWM
  N26: A1.Pin_41, Part1.D7
  N27: A1.Pin_42, Part1.D8
  N28: A1.Pin_45, Part1.D11_PWM/MOSI
  N29: A1.Pin_46, Part1.D12/MISO
  N30: A1.Pin_47, Part1.D13/SCK
  N31: A1.Pin_49, Part1.AREF

notes:
  THIS IS THE TENS UNIT

custom parts:
  Arduino UNO R4 WiFi: The Arduino UNO R4 WiFi merges the RA4M1 microprocessor from Renesas with the ESP32-S3 from Espressif, creating an all-in-one tool for makers with enhanced processing power and a diverse array of new peripherals.
